# Fritzing sketch Wiring (saved by Fritzing 0.9.3b)
breadboards: 1

parts:
  Part1 = NeoPixel Stick [part_number=1426]
  Part2 = Arduino Nano (Rev3.0)
  Power_plug1 = Power plug
  J1 = Basic Servo
  Part3 = Trellis Monochrome Driver PCB for 4x4 Keypad and 3mm LEDs [part_number=1616]
  M1 = Stepper Motor - Bipolar
  Pololu_A1 = Pololu A4988 [package=SO16]
  C1 = Electrolytic Capacitor [capacitance=1000μF package="1010 [SMD, electrolytic]"]
  Power_plug2 = Power plug
  J2 = Dagu DGServo 9g header connector (female) [package=THT]

nets:
  GND: Part1.GND, Part2.GND, Power_plug1.GND, J1.gnd, Part3.GND, Pololu_A1.GND#8
  VCC: Part1.+5V, Part2.VIN, Power_plug1.VCC, J1.vcc, Part3.VCC, Pololu_A1.VDD
  N1: Part1.DATAIN, Part2.D6
  N2: Part2.D3, Pololu_A1.ENABLE
  N3: Part2.D4, Pololu_A1.DIR
  N4: Part2.D5, Pololu_A1.STEP
  N5: Part2.D9, J1.pulse
  N6: Part2.D10, J2.pulse
  N7: Part2.A5, Part3.SCL
  N8: Part2.A4, Part3.SDA
  N9: Part2.A2, Part3.INT
  N10: M1.A, Pololu_A1.2B
  N11: M1.C, Pololu_A1.2A
  N12: M1.B, Pololu_A1.1A
  N13: M1.D, Pololu_A1.1B
  N14: Pololu_A1.RESET, Pololu_A1.SLEEP
  GND_2: Pololu_A1.GND#14, C1.+, Power_plug2.GND, J2.gnd
  VCC_2: Pololu_A1.VMOT, C1.-, Power_plug2.VCC, J2.Vcc

notes:
  5V in
  12V in
  Talon SR
  From PDP

custom parts:
  NeoPixel Stick: Make your own little LED strip arrangement with this stick of NeoPixel LEDs. We crammed 8 of the tiny 5050 (5mm x 5mm) smart RGB LEDs onto a PCB with mounting holes and a chainable design. Use only one microcontroller pin to control as many as you can chain together! Each LED is addressable as the driver chip is inside the LED. Each one has ~18mA constant current drive so the color will be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
  Trellis Monochrome Driver PCB for 4x4 Keypad and 3mm LEDs: Trellis is an open source backlight keypad driver system. It is easy to use, works with any 3mm LEDs and eight tiles can be tiled together on a shared I2C bus. This PCB is specially made to match the Adafruit 4x4 elastomer keypad. Each Trellis PCB has 4x4 pads and 4x4 matching spots for 3mm LEDs. The circuitry on-board handles the background key-presses and LED lighting for the 4x4 tile.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
